# Fritzing sketch blinker (saved by Fritzing 0.8.0b)
breadboards: 1

parts:
  Part1 = Arduino Uno (Rev3)
  LED1 = LED - 5mm [color="Red (633nm)" package="5 mm [THT]"]
  LED2 = LED - 5mm [color="Red (633nm)" package="5 mm [THT]"]
  LED3 = LED - 5mm [color="Blue (525nm)" package="5 mm [THT]"]
  LED4 = LED - 5mm [color="Blue (525nm)" package="5 mm [THT]"]
  LED5 = LED - 5mm [color="Yellow (595nm)" package="5 mm [THT]"]
  LED6 = LED - 5mm [color="Yellow (595nm)" package="5 mm [THT]"]
  LED7 = LED - 5mm [color="Green (570nm)" package="5 mm [THT]"]
  S1 = Pushbutton [package="[THT]"]
  R8 = Resistor [tolerance=±5% resistance=10k package=THT]
  R7 = Resistor [tolerance=±5% resistance=220 package=THT]
  R6 = Resistor [tolerance=±5% resistance=220 package=THT]
  R5 = Resistor [tolerance=±5% resistance=220 package=THT]
  R4 = Resistor [tolerance=±5% resistance=220 package=THT]
  R3 = Resistor [tolerance=±5% resistance=220 package=THT]
  R2 = Resistor [tolerance=±5% resistance=220 package=THT]
  R1 = Resistor [tolerance=±5% resistance=220 package=THT]

nets:
  N1: Part1.D8, LED2.anode
  N2: Part1.D9_PWM, LED4.anode
  N3: Part1.GND, R8.Pin_1, R7.Pin_1, R6.Pin_1, R5.Pin_1, R4.Pin_1, R3.Pin_1, R2.Pin_1, R1.Pin_1
  N4: Part1.D2, LED3.anode
  N5: Part1.D3_PWM, LED1.anode
  N6: Part1.D4, LED5.anode
  N7: Part1.D5_PWM, S1.Pin_1, S1.Pin_2, R8.Pin_0
  N8: Part1.D6_PWM, LED7.anode
  N9: Part1.D7, LED6.anode
  N10: Part1.5V, S1.Pin_3, S1.Pin_4
  N11: LED1.cathode, R6.Pin_0
  N12: LED2.cathode, R2.Pin_0
  N13: LED3.cathode, R7.Pin_0
  N14: LED4.cathode, R1.Pin_0
  N15: LED5.cathode, R5.Pin_0
  N16: LED6.cathode, R3.Pin_0
  N17: LED7.cathode, R4.Pin_0
