# Fritzing sketch push_button_schematics (saved by Fritzing 0.8.0b)

parts:
  Part1 = Arduino Uno (Rev3)
  R1 = Resistor [tolerance=±5% resistance=220 package=THT]
  R2 = Resistor [tolerance=±5% resistance=220 package=THT]
  R3 = Resistor [tolerance=±5% resistance=220 package=THT]
  R4 = Resistor [tolerance=±5% resistance=10k package=THT]
  S2 = Toggle Switch [package=THT]
  LED1 = RGB LED - (4 legs) [package="5 mm [THT]"]

nets:
  N1: Part1.GND, R4.Pin_1, LED1.common_anode
  N2: Part1.D13/SCK, R4.Pin_0, S2.L2
  N3: Part1.D3_PWM, R3.Pin_1
  N4: Part1.D4, R2.Pin_1
  N5: Part1.D5_PWM, R1.Pin_1
  N6: Part1.5V, S2.COM
  N7: R1.Pin_0, LED1.red_cathode
  N8: R2.Pin_0, LED1.green_cathode
  N9: R3.Pin_0, LED1.blue_cathode
